# Fritzing sketch node1 (saved by Fritzing 0.9.3b)

parts:
  Componente7 = Arduino Uno (Rev3)
  R11 = Resistor [tolerance=±5% resistance=680k package=THT]
  C5 = Electrolytic Capacitor [capacitance=47µF package="100 mil [THT, electrolytic]"]
  LED6 = LED - 5mm [color="Red (633nm)" package="5 mm [THT]"]
  R12 = Resistor [tolerance=±5% resistance=220 package=THT]
  R13 = Resistor [tolerance=±5% resistance=220 package=THT]
  M4 = Niren can bus module [package=THT]
  LED7 = LED - 5mm [color="Green (565nm)" package="5 mm [THT]"]

nets:
  N1: Componente7.A1, R11.Pin_0, C5.+
  N2: Componente7.D10_PWM/SS, M4.pin3
  N3: Componente7.D11_PWM/MOSI, M4.pin5
  N4: Componente7.D12/MISO, M4.pin4
  N5: Componente7.D13/SCK, M4.pin6
  N6: Componente7.GND, C5.-, LED6.cathode, M4.pin2, LED7.cathode
  N7: Componente7.D2, R13.Pin_1
  N8: Componente7.D3_PWM, R12.Pin_1
  N9: Componente7.D5_PWM, R11.Pin_1
  N10: Componente7.5V, M4.pin1
  N11: LED6.anode, R13.Pin_0
  N12: R12.Pin_0, LED7.anode
  N13: M4.pin8, M4.pin9

custom parts:
  Niren can bus module: Niren can bus module availabe on ebay and others. Pcb view assumes that you unsolder the 7 pin header and resolder it on the bottom of the module to connect to the pcb. The two jumpers and the can bus connector remain on the top of the board and don't appear in pcb view.
